# Fritzing sketch semaforo (saved by Fritzing 0.9.3b)
breadboards: 2

parts:
  LED5 = LED - 5mm [color="Blue (470nm)" package="5 mm [THT]"]
  LED6 = LED - 5mm [color="Red (633nm)" package="5 mm [THT]"]
  LED7 = LED - 5mm [color="Green (555nm)" package="5 mm [THT]"]
  LED8 = LED - 5mm [color="Yellow (595nm)" package="5 mm [THT]"]
  Componente1 = Arduino Uno (Rev3)
  R2 = Resistor [tolerance=±5% resistance=220 package=THT]
  R5 = Resistor [tolerance=±5% resistance=220 package=THT]
  R6 = Resistor [tolerance=±5% resistance=220 package=THT]
  R7 = Resistor [tolerance=±5% resistance=220 package=THT]
  LED9 = LED - 5mm [color="Red (633nm)" package="5 mm [THT]"]
  LED10 = LED - 5mm [color="Yellow (595nm)" package="5 mm [THT]"]
  LED11 = LED - 5mm [color="Green (555nm)" package="5 mm [THT]"]
  LED12 = LED - 5mm [color="Blue (470nm)" package="5 mm [THT]"]
  R8 = Resistor [tolerance=±5% resistance=220 package=THT]
  R9 = Resistor [tolerance=±5% resistance=220 package=THT]
  R10 = Resistor [tolerance=±5% resistance=220 package=THT]
  R11 = Resistor [tolerance=±5% resistance=220 package=THT]
  S1 = Pushbutton [package="[THT]"]
  S2 = Pushbutton [package="[THT]"]

nets:
  N1: LED5.cathode, LED6.cathode, LED7.cathode, LED8.cathode, Componente1.GND, LED9.cathode, LED10.cathode, LED11.cathode, LED12.cathode, S1.Pin_1, S1.Pin_2, S2.Pin_3, S2.Pin_4
  N2: LED5.anode, R6.Pin_1
  N3: LED6.anode, R7.Pin_1
  N4: LED7.anode, R2.Pin_1
  N5: LED8.anode, R5.Pin_1
  N6: Componente1.D8, R6.Pin_0
  N7: Componente1.D9_PWM, R7.Pin_0
  N8: Componente1.D10_PWM/SS, R5.Pin_0
  N9: Componente1.D11_PWM/MOSI, R2.Pin_0
  N10: Componente1.D13/SCK, S1.Pin_3, S1.Pin_4
  N11: Componente1.D2, S2.Pin_1, S2.Pin_2
  N12: Componente1.D4, R11.Pin_0
  N13: Componente1.D5_PWM, R8.Pin_0
  N14: Componente1.D6_PWM, R10.Pin_0
  N15: Componente1.D7, R9.Pin_0
  N16: LED9.anode, R8.Pin_1
  N17: LED10.anode, R10.Pin_1
  N18: LED11.anode, R9.Pin_1
  N19: LED12.anode, R11.Pin_1

notes:
  Av. Principal
  Av. Secundaria

// code stored in the sketch: semaforo.ino
/*****************************************************
								Desafio#1 - Platzi
	Semáforo para dos Avenidas (Principal y Secundaria)
	ambas tienen una luz azul para indicar el giro a la
	izquierda y un pulsador peatonal para cambiar el 
	estado de la luz verde y darle paso a los peatones.

	Configuración:
		Entradas: botones peatonales {13(P),2(S)} 
		Salidas: 
			luces verde, amarilla, roja y azul 
						{11,10,9,8}Princial ; {7,6,5,4}Secundaria

	Autor: Pablo Cardozo

*****************************************************/
// Avenida Principal
const int vp = 11;
const int ap = 10;
const int rp = 9;
const int zp = 8;
const int butP = 13;	//Pulsador Peatonal
const int semP[4] = {vp, ap, rp, zp};	// arreglo para semáforo Principal
// Avenida Secundaria
const int vs = 7;
const int as = 6;
const int rs = 5;
const int zs = 4;
const int butS = 2;	//Pulsador Peatonal
const int semS[4] = {vs, as, rs, zs}; // arreglo para semáforo Secundario
// Tiempos para cada luz en milisegundos (tr = tz)
int ta = 2000;
int tv = 6000;
int tz = 3000;
// Variables Globales
unsigned long tiempoActual;
int tiempo;
int estadoSem;	// el semáforo tiene 6 estados
bool flagButton = false;


void setup()
{
	// Configuración de Salidas para los semáforos
	for(int i=0; i<4; i++){
		pinMode(semP[i], OUTPUT);    
		pinMode(semS[i], OUTPUT);    
	}
	// Configuración de Entradas para los pulsadores
	pinMode(butP, INPUT_PULLUP);
	pinMode(butS, INPUT_PULLUP);

	iniciar();
}

void loop()
{
	if((millis() - tiempoActual) > tiempo) {
		cambio();
		tiempoActual = millis();
	}
	if((digitalRead(butP) == LOW) || (digitalRead(butS) == LOW)) {		
		delay(200);
		//esperamos hasta que los botones no esten pulsados
		while((digitalRead(butP) == LOW) && (digitalRead(butS) == LOW));		
		flagButton = true;
		estadoSem--;	// el estado actual apunta al siguiente
		if(estadoSem <= 0)	estadoSem = 6;
		if((estadoSem == 1) || (estadoSem == 4))	estadoSem++, cambio();
		else flagButton = false;
		tiempoActual = millis();		
	}
}

void iniciar() {	
	estadoSem = 1;
	cambio();
}

void cambio() {
	for(int i=0; i<4; i++) {
		digitalWrite(semP[i], LOW);    
		digitalWrite(semS[i], LOW);    
	}
	switch (estadoSem) {
	    case 1:
	      digitalWrite(vp, HIGH);
	      digitalWrite(rs, HIGH);
	      tiempo = tv;
	      break;
	    case 2:
	      digitalWrite(ap, HIGH);
	      digitalWrite(rs, HIGH);
	      tiempo = ta;
	      break;
	    case 3:
	      digitalWrite(rp, HIGH);
	      digitalWrite(zp, HIGH);
	      digitalWrite(rs, HIGH);
	      tiempo = tz;
	      break;
	    case 4:
	      digitalWrite(rp, HIGH);
	      digitalWrite(vs, HIGH);
	      tiempo = tv;
	      break;
	    case 5:
	      digitalWrite(rp, HIGH);
	      digitalWrite(as, HIGH);
	      tiempo = ta;
	      break;
	    case 6:
	      digitalWrite(rp, HIGH);
	      digitalWrite(rs, HIGH);
	      digitalWrite(zs, HIGH);
	      tiempo = tz;
	      break;
	    default:
	      break;
	}
	if(flagButton)	estadoSem += 2, flagButton = false;
	else estadoSem++;
	if(estadoSem > 6)	estadoSem = 1;
}
